# Fritzing sketch project (saved by Fritzing 0.9.3b)
breadboards: 1

parts:
  Part1 = Arduino Uno (Rev3)
  M1 = ESP-01 Breakout Board Breadboard Adapter [part_number=ESP8266]
  U2 = GAS_SENSOR [package=mq-3]
  DHT2 = DHT11 Humitidy and Temperature Sensor (3 pins)

nets:
  N1: Part1.A0, DHT2.VDD
  N2: Part1.A1, U2.A1
  GND: Part1.GND, M1.GND, U2.B1, DHT2.GND
  N3: Part1.D2, M1.TXD
  N4: Part1.D3_PWM, M1.RXD
  5V: Part1.5V, M1.VCC, DHT2.DATA

custom parts:
  ESP-01 Breakout Board Breadboard Adapter: Generic WiFi Module based on the ESP8266 with onboard PCB antenna and UART communications with breadboard friendly breakout board attached.
  DHT11 Humitidy and Temperature Sensor (3 pins): DHT11 Humidity and Temperature Sensor (3 pins) from the design created by John De Cristofaro for Adafruit Industries.
